# Fritzing sketch bot (saved by Fritzing 0.9.6b)

parts:
  U1 = ESP8266 NodeMCU LoLin module
  HC-SR04_Sensor_1 = HC-SR04 Ultrasonic Distance Sensor
  M1 = gear-motor
  M2 = gear-motor
  VCC1 = 4 x AAA Battery Mount
  U2 = L9110 H-bridge module [part_number="L9110 H-bridge"]

nets:
  N1: U1.D1, U2.A-IB
  N2: U1.D3, HC-SR04_Sensor_1.TRIG
  N3: U1.D4, HC-SR04_Sensor_1.ECHO
  N4: U1.D5, U2.B-IA
  N5: U1.D6, U2.B-IB
  N6: U1.D7, U2.A-IA
  VCC: U1.Vin, HC-SR04_Sensor_1.VCC, VCC1.+, U2.VCC
  N7: M1.pin_1, U2.MOTOR_A-B
  N8: M1.pin_2, U2.MOTOR_A-A
  N9: M2.pin_1, U2.MOTOR_B-B
  N10: M2.pin_2, U2.MOTOR_B-A

custom parts:
  ESP8266 NodeMCU LoLin module: ESP8266 based NodeMCU
